// Logisim project 523H0102.circ as structural Verilog
module _2_to_1_MUX (
  input  I0,
  input  A,
  input  I1,
  output Q
);

  wire and_1_out, and_2_out, and_3_out, and_4_out, not_1_out, not_2_out, not_3_out;

  and and_1 (and_1_out, A, A);
  not not_1 (not_1_out, and_1_out);
  not not_2 (not_2_out, and_2_out);
  and and_2 (and_2_out, I0, A);
  and and_3 (and_3_out, not_1_out, I1);
  not not_3 (not_3_out, and_3_out);
  and and_4 (and_4_out, not_2_out, not_3_out);
  not not_4 (Q, and_4_out);

  // Notes on the sheet:
  //   I0
  //   A
  //   A'
  //   I1
  //   Ngô Chí Thuận
  //   2-to-1 MUX
endmodule

module _4_to_1_MUX (
  input  A,
  input  B,
  input  C,
  input  D,
  input  b_2,
  input  a_2,
  output Q
);

  wire and_1_out, and_2_out, and_3_out, and_4_out, and_5_out, and_6_out, and_7_out, not_1_out, not_2_out,
       not_3_out, not_4_out, not_5_out, not_6_out;

  and and_1 (and_1_out, b_2, b_2);
  and and_2 (and_2_out, a_2, a_2);
  not not_1 (not_1_out, and_1_out);
  not not_2 (not_2_out, and_2_out);
  and and_3 (and_3_out, A, not_1_out, not_2_out);
  not not_3 (not_3_out, and_3_out);
  not not_4 (not_4_out, and_4_out);
  and and_4 (and_4_out, B, not_1_out, a_2);
  not not_5 (not_5_out, and_5_out);
  and and_5 (and_5_out, C, b_2);
  not not_6 (not_6_out, and_6_out);
  and and_6 (and_6_out, D, b_2, a_2);
  not not_7 (Q, and_7_out);
  and and_7 (and_7_out, not_3_out, not_4_out, not_5_out, not_6_out);

  // Notes on the sheet:
  //   Data Inuts
  //   Select
  //   b'
  //   a'
  //   Ngô Chí Thuận
  //   NAND
  //   Gates
endmodule

module _8_to_1_MUX (
  input  A,
  input  B,
  input  C,
  input  D,
  input  a_2,
  input  b_2,
  input  E,
  input  F,
  input  G,
  input  e_2,
  input  H,
  input  c_2,
  input  d_2,
  output Q
);

  wire n4_to_1_mux_1_q, n4_to_1_mux_2_q;

  _4_to_1_MUX u_4_to_1_mux_1 (.A(A), .B(B), .C(C), .D(D), .b_2(a_2), .a_2(b_2), .Q(n4_to_1_mux_1_q));
  _4_to_1_MUX u_4_to_1_mux_2 (.A(E), .B(F), .C(G), .D(H), .b_2(c_2), .a_2(d_2), .Q(n4_to_1_mux_2_q));
  _2_to_1_MUX u_2_to_1_mux_1 (.I0(n4_to_1_mux_1_q), .A(n4_to_1_mux_2_q), .I1(e_2), .Q(Q));

  // Notes on the sheet:
  //   Ngô Chí Thuận
endmodule

module _4_to_1_DEMUX (
  input  a,
  input  b,
  input  F,
  output A_2,
  output B_2,
  output C,
  output D
);

  wire not_1_out, not_2_out;

  not not_1 (not_1_out, a);
  not not_2 (not_2_out, b);
  and and_1 (A_2, F, F, a, not_1_out);
  and and_2 (B_2, F, not_2_out, a);
  and and_3 (C, F, b, not_1_out);
  and and_4 (D, F, b, a);

  // Notes on the sheet:
  //   Ngô Chí Thuận
endmodule

module _4_to_2_Encoder (
  input  D,
  input  C,
  input  B,
  input  A,
  output X,
  output Y
);

  or or_1 (X, D, C);
  or or_2 (Y, D, B);

  // Notes on the sheet:
  //   Ngô Chí Thuận
endmodule

module _8_to_3_Bit_Priority_Encoder (
  input  in_1,
  input  in_2,
  input  in_3,
  input  in_4,
  input  in_5,
  input  in_6,
  input  in_7,
  input  in_8,
  output X,
  output Y,
  output Z
);

  or or_1 (X, in_4, in_3, in_2, in_1);
  or or_2 (Y, in_6, in_5, in_2, in_1);
  or or_3 (Z, in_7, in_5, in_3, in_1);

  // Notes on the sheet:
  //   A        B       C       D       E       F      G       H 
  //   Ngô Chí Thuận
endmodule
