// Logisim project 1logi.circ as structural Verilog: 2 circuits, main circuit main
module main (
  input  in_1
);

  wire and_1_out, and_2_out, and_3_out, and_4_out, clock_1_out, decoder_1_out_5, decoder_1_out_6,
       decoder_1_out_7, decoder_1_out_8, decoder_1_out_9, decoder_1_out_10, decoder_1_out_11, j_k_ff_1_q,
       j_k_ff_1_qn, j_k_ff_2_q, j_k_ff_3_q, j_k_ff_3_qn, j_k_ff_4_q;

  Clock clock_1 (.out(clock_1_out));
  and and_1 (and_1_out, j_k_ff_4_q, j_k_ff_3_q, j_k_ff_2_q);
  and and_2 (and_2_out, j_k_ff_3_qn, j_k_ff_4_q);
  J_K_Flip_Flop j_k_ff_1 (
    .J(and_1_out), .clk(clock_1_out), .K(and_2_out), .Q(j_k_ff_1_q), .Qn(j_k_ff_1_qn));  // open: preset, en, reset
  and and_3 (and_3_out, j_k_ff_4_q, j_k_ff_3_q);
  J_K_Flip_Flop j_k_ff_2 (
    .J(and_3_out), .clk(clock_1_out), .K(and_3_out), .Q(j_k_ff_2_q));  // open: Qn, preset, en, reset
  and and_4 (and_4_out, j_k_ff_1_qn, j_k_ff_4_q);
  J_K_Flip_Flop j_k_ff_3 (
    .J(and_4_out), .clk(clock_1_out), .K(j_k_ff_4_q), .Q(j_k_ff_3_q), .Qn(j_k_ff_3_qn));  // open: preset, en, reset
  J_K_Flip_Flop j_k_ff_4 (.J(in_1), .clk(clock_1_out), .K(in_1), .Q(j_k_ff_4_q));  // open: Qn, preset, en, reset
  decoder decoder_1 (
    .in_1(j_k_ff_1_q), .in_2(j_k_ff_2_q), .in_3(j_k_ff_3_q), .in_4(j_k_ff_4_q), .out_5(decoder_1_out_5),
    .out_6(decoder_1_out_6), .out_7(decoder_1_out_7), .out_8(decoder_1_out_8), .out_9(decoder_1_out_9),
    .out_10(decoder_1_out_10), .out_11(decoder_1_out_11));
  _7_Segment_Display u_7_segment_display_1 (
    .g(decoder_1_out_11), .f(decoder_1_out_10), .a(decoder_1_out_5), .b(decoder_1_out_6),
    .e(decoder_1_out_9), .d(decoder_1_out_8), .c(decoder_1_out_7));  // open: dp
endmodule

module decoder (
  input  in_1,
  input  in_2,
  input  in_3,
  input  in_4,
  output out_5,
  output out_6,
  output out_7,
  output out_8,
  output out_9,
  output out_10,
  output out_11
);

  wire and_1_out, and_2_out, and_3_out, and_4_out, and_5_out, and_6_out, and_7_out, and_8_out, not_1_out,
       not_2_out, not_3_out, not_4_out, not_5_out, not_6_out, not_7_out, not_8_out, not_9_out, not_10_out,
       not_11_out, not_12_out, not_13_out, or_1_out, or_2_out, or_3_out, xnor_1_out, xor_1_out;

  not not_1 (not_1_out, in_1);
  not not_2 (not_2_out, in_2);
  not not_3 (not_3_out, in_4);
  not not_4 (not_4_out, in_2);
  and and_1 (and_1_out, in_4, in_2);
  and and_2 (and_2_out, not_1_out, not_2_out, not_3_out);
  or or_1 (or_1_out, not_4_out, in_3);
  not not_5 (not_5_out, in_2);
  not not_6 (not_6_out, in_4);
  not not_7 (not_7_out, in_2);
  not not_8 (not_8_out, in_4);
  not not_9 (not_9_out, in_3);
  not not_10 (not_10_out, in_2);
  or or_2 (or_2_out, not_5_out, not_6_out);
  not not_11 (not_11_out, in_2);
  xnor xnor_1 (xnor_1_out, in_4, in_3);
  not not_12 (not_12_out, in_3);
  and and_3 (and_3_out, not_7_out, in_3);
  and and_4 (and_4_out, or_1_out, not_8_out);
  and and_5 (and_5_out, in_2, not_9_out, in_4);
  or or_3 (or_3_out, not_10_out, in_3);
  not not_13 (not_13_out, in_4);
  and and_6 (and_6_out, in_2, or_2_out);
  and and_7 (and_7_out, not_5_out, not_6_out);
  and and_8 (and_8_out, in_2, not_6_out);
  xor xor_1 (xor_1_out, in_2, in_3);
  or or_4 (out_5, in_1, and_1_out, in_3, and_2_out);
  or or_5 (out_6, not_11_out, xnor_1_out);
  or or_6 (out_7, in_1, in_2, not_12_out, in_4);
  or or_7 (out_8, in_1, and_3_out, and_4_out, and_5_out);
  and and_9 (out_9, or_3_out, not_13_out);
  or or_8 (out_10, in_1, and_6_out, and_7_out);
  or or_9 (out_11, in_1, and_8_out, xor_1_out);
endmodule
