// Logisim project 523H0094 (1).circ as structural Verilog
module _2_1_MUX (
  input  IN_0,
  input  IN_1,
  input  SELECT,
  output OUT
);

  wire and_1_out, and_2_out, not_1_out;

  and and_1 (and_1_out, IN_0, not_1_out);
  not not_1 (not_1_out, SELECT);
  and and_2 (and_2_out, IN_1, SELECT);
  or or_1 (OUT, and_1_out, and_2_out);
endmodule

module _4_1_MUX (
  input  a,
  input  b,
  input  c,
  input  d,
  input  e,
  input  f,
  output OUT
);

  wire n2_1_mux_2_out, n2_1_mux_3_out;

  _2_1_MUX u_2_1_mux_1 (.IN_0(n2_1_mux_2_out), .IN_1(n2_1_mux_3_out), .SELECT(e), .OUT(OUT));
  _2_1_MUX u_2_1_mux_2 (.IN_0(a), .IN_1(b), .SELECT(f), .OUT(n2_1_mux_2_out));
  _2_1_MUX u_2_1_mux_3 (.IN_0(c), .IN_1(d), .SELECT(f), .OUT(n2_1_mux_3_out));
endmodule

module HALF_ADDER (
  input  A,
  input  B,
  output Z,
  output COUNT
);

  xor xor_1 (Z, A, B);
  and and_1 (COUNT, B, A);
endmodule

module FULL_ADDER (
  input  A,
  input  B,
  input  C,
  output SUM,
  output COUNT
);

  wire half_adder_1_count, half_adder_1_z, half_adder_2_count;

  HALF_ADDER half_adder_1 (.A(A), .B(B), .Z(half_adder_1_z), .COUNT(half_adder_1_count));
  HALF_ADDER half_adder_2 (.A(half_adder_1_z), .B(C), .Z(SUM), .COUNT(half_adder_2_count));
  or or_1 (COUNT, half_adder_2_count, half_adder_1_count);

  // Notes on the sheet:
  //   HALF ADDER
  //   HALF ADDER
endmodule

module _2_BIT_ADDER (
  input  [1:0] A,
  input  [1:0] B,
  input  C,
  output OUT_0,
  output [1:0] out_5
);

  wire full_adder_1_sum;

  FULL_ADDER full_adder_1 (.A(A[0]), .B(B[0]), .C(C), .SUM(full_adder_1_sum), .COUNT(out_5[1]));
  FULL_ADDER full_adder_2 (.A(full_adder_1_sum), .B(B[1]), .C(A[1]), .SUM(OUT_0), .COUNT(out_5[0]));

  // Notes on the sheet:
  //   FULL ADDER
  //   FULL ADDER
  //   COUNT
endmodule

module _4_1_BIT_ADDER (
  input  A,
  input  B,
  input  C,
  output out_4,
  output out_5
);

  wire full_adder_1_count, full_adder_1_sum, full_adder_2_count, full_adder_2_sum, full_adder_3_count,
       full_adder_3_sum, full_adder_4_count;

  FULL_ADDER full_adder_1 (.A(A), .B(B), .C(C), .SUM(full_adder_1_sum), .COUNT(full_adder_1_count));
  FULL_ADDER full_adder_2 (.A(full_adder_1_sum), .B(A), .C(B), .SUM(full_adder_2_sum), .COUNT(full_adder_2_count));
  FULL_ADDER full_adder_3 (.A(full_adder_2_sum), .B(A), .C(B), .SUM(full_adder_3_sum), .COUNT(full_adder_3_count));
  FULL_ADDER full_adder_4 (.A(full_adder_3_sum), .B(A), .C(B), .SUM(out_4), .COUNT(full_adder_4_count));
  or or_1 (out_5, full_adder_4_count, full_adder_3_count, full_adder_2_count, full_adder_1_count);

  // Notes on the sheet:
  //   full adder
  //   full adder
  //   full adder
  //   full adder
endmodule

module _8_1_BIT_ADDER (
  input  in_1,
  input  in_2,
  input  in_3,
  output out_4
);

  wire full_adder_1_count, full_adder_1_sum, full_adder_2_count, full_adder_2_sum, full_adder_3_count,
       full_adder_3_sum, full_adder_4_count, full_adder_4_sum, full_adder_5_count, full_adder_5_sum,
       full_adder_6_count, full_adder_6_sum, full_adder_7_count, full_adder_7_sum, full_adder_8_count;

  FULL_ADDER full_adder_1 (.A(in_1), .B(in_1), .C(in_3), .SUM(full_adder_1_sum), .COUNT(full_adder_1_count));
  FULL_ADDER full_adder_2 (
    .A(full_adder_7_sum), .B(in_1), .C(in_1), .SUM(full_adder_2_sum), .COUNT(full_adder_2_count));
  FULL_ADDER full_adder_3 (
    .A(full_adder_1_sum), .B(in_1), .C(in_1), .SUM(full_adder_3_sum), .COUNT(full_adder_3_count));
  FULL_ADDER full_adder_4 (
    .A(full_adder_2_sum), .B(in_1), .C(in_1), .SUM(full_adder_4_sum), .COUNT(full_adder_4_count));
  FULL_ADDER full_adder_5 (
    .A(full_adder_3_sum), .B(in_1), .C(in_1), .SUM(full_adder_5_sum), .COUNT(full_adder_5_count));
  FULL_ADDER full_adder_6 (
    .A(full_adder_4_sum), .B(in_1), .C(in_1), .SUM(full_adder_6_sum), .COUNT(full_adder_6_count));
  FULL_ADDER full_adder_7 (
    .A(full_adder_5_sum), .B(in_1), .C(in_1), .SUM(full_adder_7_sum), .COUNT(full_adder_7_count));
  FULL_ADDER full_adder_8 (.A(full_adder_6_sum), .B(in_1), .C(in_1), .SUM(out_4), .COUNT(full_adder_8_count));

  assign in_2 = in_1;
endmodule

module _8_to_1_MUX (
  input  [3:0] d4,
  input  [1:0] in_2,
  input  select,
  input  [3:0] d8,
  input  [1:0] select_2,
  output _2_1_Mux
);

  wire n4_1_mux_1_out, n4_1_mux_2_out;

  _4_1_MUX u_4_1_mux_1 (.a(d4[0]), .b(d4[1]), .c(d4[2]), .d(d4[3]), .e(in_2[1]), .f(in_2[0]), .OUT(n4_1_mux_1_out));
  _4_1_MUX u_4_1_mux_2 (
    .a(d8[0]), .b(d8[1]), .c(d8[2]), .d(d8[3]), .e(select_2[1]), .f(select_2[0]), .OUT(n4_1_mux_2_out));
  _2_1_MUX u_2_1_mux_1 (.IN_0(n4_1_mux_1_out), .IN_1(n4_1_mux_2_out), .SELECT(select), .OUT(_2_1_Mux));

  // Notes on the sheet:
  //   d0
  //   d1
  //   d2
  //   d5
  //   d6
  //   d7
  //   Nguyễn Quốc Thắng
  //   4:1 Mux
  //   select
  //   4:1 Mux
endmodule

module _8_to_2 (
  input  [3:0] in_1,
  input  [3:0] in_2,
  input  in_3,
  input  in_4,
  output out_5,
  output out_6
);

  _4_1_MUX u_4_1_mux_1 (.a(in_1[0]), .b(in_1[1]), .c(in_1[2]), .d(in_1[3]), .e(in_3), .f(in_4), .OUT(out_5));
  _4_1_MUX u_4_1_mux_2 (.a(in_2[0]), .b(in_2[1]), .c(in_2[2]), .d(in_2[3]), .e(in_3), .f(in_4), .OUT(out_6));

  // Notes on the sheet:
  //   Nguyễn Quốc Thắng
endmodule

module Demux_1_4 (
  input  a,
  input  b,
  input  c,
  output A_2,
  output B_2,
  output C_2,
  output D
);

  wire not_1_out, not_2_out;

  not not_1 (not_1_out, a);
  not not_2 (not_2_out, b);
  and and_1 (A_2, not_2_out, c, not_1_out);
  and and_2 (B_2, c, c, a, not_2_out);
  and and_3 (C_2, not_1_out, c, b);
  and and_4 (D, a, b, c);

  // Notes on the sheet:
  //   Nguyễn Quốc Thắng
endmodule

module SR_Flip__fLop (
  input  in_1,
  input  R_prime,
  output Q,
  output Q_prime
);

  nand nand_1 (Q, in_1, Q_prime);
  nand nand_2 (Q_prime, Q, R_prime);

  // Notes on the sheet:
  //   S'
  //   Nguyễn Quốc Thắng
endmodule

module RS_Lacth (
  input  in_1,
  input  R_prime,
  output Q,
  output Q_prime
);

  nor nor_1 (Q, in_1, Q_prime);
  nor nor_2 (Q_prime, Q, R_prime);

  // Notes on the sheet:
  //   S'
  //   Nguyễn Quốc Thắng
endmodule

module The_Clocked_SR_Flip_Flop (
  input  S,
  input  CK,
  input  R,
  output Q,
  output Q_prime
);

  wire nand_1_out, nand_2_out;

  nand nand_1 (nand_1_out, S, S, CK);
  nand nand_2 (nand_2_out, CK, R);
  nand nand_3 (Q, nand_1_out, Q_prime);
  nand nand_4 (Q_prime, Q, nand_2_out);

  // Notes on the sheet:
  //   Nguyễn Quốc Thắng
endmodule

module D_flip_flop (
  input  D,
  input  in_2,
  output Q,
  output Q_prime
);

  wire nand_1_out;

  nand nand_1 (nand_1_out, D, D);
  The_Clocked_SR_Flip_Flop the_clocked_sr_flip_flop_1 (.S(D), .CK(in_2), .R(nand_1_out), .Q(Q), .Q_prime(Q_prime));

  // Notes on the sheet:
  //   CK
  //   NGUYỄN QUỐC THẮNG
  //   THE CLOCKED SR FLIP FLOPS
endmodule

module D_Latch_with_Set_Reset_inputs (
  output out_1,
  output out_2
);

  wire clock_1_out, clock_2_out, d_ff_1_qn, d_latch_1_q_prime;

  Clock clock_1 (.out(clock_1_out));
  Clock clock_2 (.out(clock_2_out));
  D_Flip_Flop d_ff_1 (.clk(clock_1_out), .D(d_ff_1_qn), .Q(out_1), .Qn(d_ff_1_qn));  // open: preset, en, reset
  D_LATCH d_latch_1 (.D(clock_2_out), .CK(d_latch_1_q_prime), .Q(out_2), .Q_prime(d_latch_1_q_prime));

  // Notes on the sheet:
  //   NGUYỄN QUỐC THẮNG
endmodule

module JK_Flip_flops (
  input  J,
  input  CK,
  input  K,
  output Q,
  output Q_prime
);

  wire NAND1_out, NAND2_out;

  nand NAND1 (NAND1_out, Q_prime, J, CK);
  nand NAND2 (NAND2_out, CK, K, Q);
  nand nand_1 (Q, NAND1_out, Q_prime);
  nand nand_2 (Q_prime, Q, NAND2_out);
endmodule

module test_Clocked_SR__Flip_Flop (
  input  in_1,
  input  in_2,
  output out_3,
  output out_4
);

  wire clock_1_out;

  Clock clock_1 (.out(clock_1_out));
  The_Clocked_SR_Flip_Flop the_clocked_sr_flip_flop_1 (
    .S(in_1), .CK(clock_1_out), .R(in_2), .Q(out_3), .Q_prime(out_4));

  // Notes on the sheet:
  //   NGUYỄN QUỐC THẮNG
endmodule

module D_LATCH (
  input  D,
  input  CK,
  output Q,
  output Q_prime
);

  wire nand_1_out, nand_2_out, not_1_out;

  not not_1 (not_1_out, D);
  nand nand_1 (nand_1_out, D, CK);
  nand nand_2 (nand_2_out, CK, not_1_out, not_1_out);
  nor nor_1 (Q, nand_1_out, Q_prime);
  nor nor_2 (Q_prime, Q, nand_2_out);

  // Notes on the sheet:
  //   NGUYỄN QUỐC THẮNG
endmodule

module TEST_J_K_filp_flop_as_a_sub_circuit (
  input  in_1,
  input  in_2,
  output out_3,
  output out_4
);

  wire clock_1_out;

  Clock clock_1 (.out(clock_1_out));
  JK_Flip_flops jk_flip_flops_1 (.J(in_1), .CK(clock_1_out), .K(in_2), .Q(out_3), .Q_prime(out_4));
endmodule

module Four_bit_Asynchronous_Up_Counter (
);

  wire and_1_out, clock_1_out, d_ff_1_qn, d_ff_2_qn, d_ff_3_qn, d_ff_4_qn;
  wire [3:0] d_ff_1_q;

  Clock clock_1 (.out(clock_1_out));
  D_Flip_Flop d_ff_1 (
    .clk(clock_1_out), .D(d_ff_1_qn), .Q(d_ff_1_q[0]), .Qn(d_ff_1_qn), .reset(and_1_out));  // open: preset, en
  D_Flip_Flop d_ff_2 (
    .clk(d_ff_1_qn), .D(d_ff_2_qn), .Q(d_ff_1_q[1]), .Qn(d_ff_2_qn), .reset(and_1_out));  // open: preset, en
  Hex_Digit_Display hex_digit_display_1 (.value(d_ff_1_q));  // open: dp
  and and_1 (and_1_out, d_ff_1_q[1], d_ff_1_q[3]);
  D_Flip_Flop d_ff_3 (
    .clk(d_ff_2_qn), .D(d_ff_3_qn), .Q(d_ff_1_q[2]), .Qn(d_ff_3_qn), .reset(and_1_out));  // open: preset, en
  D_Flip_Flop d_ff_4 (
    .clk(d_ff_3_qn), .D(d_ff_4_qn), .Q(d_ff_1_q[3]), .Qn(d_ff_4_qn), .reset(and_1_out));  // open: preset, en

  // Notes on the sheet:
  //   Nguyễn Quốc Thắng
endmodule

module _5_6_3_Four_bit_Asynchronous_Down_Counter (
);

  wire clock_1_out, d_ff_1_qn, d_ff_2_qn, d_ff_3_qn, d_ff_4_qn, undriven;
  wire [3:0] d_ff_4_q;

  Clock clock_1 (.out(clock_1_out));
  D_Flip_Flop d_ff_1 (.clk(clock_1_out), .D(d_ff_1_qn), .Q(d_ff_4_q[3]), .Qn(d_ff_1_qn));  // open: preset, en, reset
  D_Flip_Flop d_ff_2 (.clk(d_ff_4_q[3]), .D(d_ff_2_qn), .Q(d_ff_4_q[2]), .Qn(d_ff_2_qn));  // open: preset, en, reset
  Hex_Digit_Display hex_digit_display_1 (.value(d_ff_4_q));  // open: dp
  D_Flip_Flop d_ff_3 (
    .clk(d_ff_4_q[2]), .D(d_ff_3_qn), .Q(d_ff_4_q[1]), .Qn(d_ff_3_qn), .reset(undriven));  // open: preset, en
  D_Flip_Flop d_ff_4 (.clk(d_ff_4_q[1]), .D(d_ff_4_qn), .Q(d_ff_4_q[0]), .Qn(d_ff_4_qn));  // open: preset, en, reset
endmodule

module Four_Bit_Synchronous_Up_Counter (
);

  wire and_1_out, and_2_out, clock_1_out, j_k_ff_1_qn, j_k_ff_2_qn, j_k_ff_3_qn, j_k_ff_4_qn, not_1_out,
       not_2_out;
  wire [3:0] j_k_ff_1_q;

  not not_1 (not_1_out, 1'b1);
  not not_2 (not_2_out, 1'b1);
  Clock clock_1 (.out(clock_1_out));
  J_K_Flip_Flop j_k_ff_1 (
    .J(1'b1), .clk(clock_1_out), .K(1'b1), .Q(j_k_ff_1_q[0]), .Qn(j_k_ff_1_qn), .preset(not_2_out),
    .reset(not_1_out));  // open: en
  J_K_Flip_Flop j_k_ff_2 (
    .J(j_k_ff_1_q[0]), .clk(clock_1_out), .K(j_k_ff_1_q[0]), .Q(j_k_ff_1_q[1]), .Qn(j_k_ff_2_qn),
    .preset(not_2_out), .reset(not_1_out));  // open: en
  Hex_Digit_Display hex_digit_display_1 (.value(j_k_ff_1_q));  // open: dp
  and and_1 (and_1_out, j_k_ff_1_q[0], j_k_ff_1_q[1]);
  J_K_Flip_Flop j_k_ff_3 (
    .J(and_1_out), .clk(clock_1_out), .K(and_1_out), .Q(j_k_ff_1_q[2]), .Qn(j_k_ff_3_qn), .preset(not_2_out),
    .reset(not_1_out));  // open: en
  and and_2 (and_2_out, and_1_out, j_k_ff_1_q[2]);
  J_K_Flip_Flop j_k_ff_4 (
    .J(and_2_out), .clk(clock_1_out), .K(and_2_out), .Q(j_k_ff_1_q[3]), .Qn(j_k_ff_4_qn), .preset(not_2_out),
    .reset(not_1_out));  // open: en
endmodule

module Four_Bit_Synchronous_Down_Counter (
);

  wire and_1_out, and_2_out, clock_1_out, j_k_ff_1_qn, j_k_ff_2_qn, j_k_ff_3_qn, j_k_ff_4_qn, not_1_out,
       not_2_out;
  wire [3:0] j_k_ff_1_q;

  not not_1 (not_1_out, 1'b1);
  not not_2 (not_2_out, 1'b1);
  Clock clock_1 (.out(clock_1_out));
  J_K_Flip_Flop j_k_ff_1 (
    .J(1'b1), .clk(clock_1_out), .K(1'b1), .Q(j_k_ff_1_q[0]), .Qn(j_k_ff_1_qn), .preset(not_2_out),
    .reset(not_1_out));  // open: en
  J_K_Flip_Flop j_k_ff_2 (
    .J(j_k_ff_1_q[0]), .clk(clock_1_out), .K(j_k_ff_1_q[0]), .Q(j_k_ff_1_q[1]), .Qn(j_k_ff_2_qn),
    .preset(not_2_out), .reset(not_1_out));  // open: en
  Hex_Digit_Display hex_digit_display_1 (.value(j_k_ff_1_q));  // open: dp
  and and_1 (and_1_out, j_k_ff_1_q[0], j_k_ff_1_q[1]);
  J_K_Flip_Flop j_k_ff_3 (
    .J(and_1_out), .clk(clock_1_out), .K(and_1_out), .Q(j_k_ff_1_q[2]), .Qn(j_k_ff_3_qn), .preset(not_2_out),
    .reset(not_1_out));  // open: en
  and and_2 (and_2_out, and_1_out, j_k_ff_1_q[2]);
  J_K_Flip_Flop j_k_ff_4 (
    .J(and_2_out), .clk(clock_1_out), .K(and_2_out), .Q(j_k_ff_1_q[3]), .Qn(j_k_ff_4_qn), .preset(not_2_out),
    .reset(not_1_out));  // open: en
endmodule

module Four_bit_Synchronous_Up_Down_Counter (
  input  in_1
);

  wire and_1_out, and_2_out, and_3_out, and_4_out, and_5_out, and_6_out, clock_1_out, j_k_ff_1_qn,
       j_k_ff_2_qn, j_k_ff_3_qn, j_k_ff_4_qn, not_1_out, not_2_out, not_3_out, not_4_out, or_1_out, or_2_out,
       or_3_out;
  wire [3:0] j_k_ff_1_q;

  Clock clock_1 (.out(clock_1_out));
  not not_1 (not_1_out, not_2_out);
  not not_2 (not_2_out, in_1);
  not not_3 (not_3_out, 1'b1);
  not not_4 (not_4_out, 1'b1);
  Hex_Digit_Display hex_digit_display_1 (.value(j_k_ff_1_q));  // open: dp
  and and_1 (and_1_out, j_k_ff_1_q[0], not_1_out);
  and and_2 (and_2_out, not_2_out, j_k_ff_1_qn);
  J_K_Flip_Flop j_k_ff_1 (
    .J(1'b1), .clk(clock_1_out), .K(1'b1), .Q(j_k_ff_1_q[0]), .Qn(j_k_ff_1_qn), .preset(not_4_out),
    .reset(not_3_out));  // open: en
  or or_1 (or_1_out, and_1_out, and_2_out);
  J_K_Flip_Flop j_k_ff_2 (
    .J(or_1_out), .clk(clock_1_out), .K(or_1_out), .Q(j_k_ff_1_q[1]), .Qn(j_k_ff_2_qn), .preset(not_4_out),
    .reset(not_3_out));  // open: en
  and and_3 (and_3_out, and_1_out, j_k_ff_1_q[1]);
  and and_4 (and_4_out, and_2_out, j_k_ff_2_qn);
  or or_2 (or_2_out, and_3_out, and_4_out);
  J_K_Flip_Flop j_k_ff_3 (
    .J(or_2_out), .clk(clock_1_out), .K(or_2_out), .Q(j_k_ff_1_q[2]), .Qn(j_k_ff_3_qn), .preset(not_4_out),
    .reset(not_3_out));  // open: en
  and and_5 (and_5_out, and_3_out, j_k_ff_1_q[2]);
  and and_6 (and_6_out, and_4_out, j_k_ff_3_qn);
  J_K_Flip_Flop j_k_ff_4 (
    .J(or_3_out), .clk(clock_1_out), .K(or_3_out), .Q(j_k_ff_1_q[3]), .Qn(j_k_ff_4_qn), .preset(not_4_out),
    .reset(not_3_out));  // open: en
  or or_3 (or_3_out, and_5_out, and_6_out);
endmodule

module _9_0 (
);

  wire and_1_out, and_2_out, and_3_out, and_4_out, clock_1_out, j_k_ff_1_qn, j_k_ff_2_qn, j_k_ff_3_qn,
       j_k_ff_4_qn, or_1_out;
  wire [3:0] j_k_ff_1_q;

  Clock clock_1 (.out(clock_1_out));
  J_K_Flip_Flop j_k_ff_1 (
    .J(1'b1), .clk(clock_1_out), .K(1'b1), .Q(j_k_ff_1_q[0]), .Qn(j_k_ff_1_qn));  // open: preset, en, reset
  and and_1 (and_1_out, j_k_ff_1_qn, j_k_ff_2_qn);
  and and_2 (and_2_out, and_1_out, or_1_out);
  J_K_Flip_Flop j_k_ff_2 (
    .J(and_2_out), .clk(clock_1_out), .K(j_k_ff_1_qn), .Q(j_k_ff_1_q[1]), .Qn(j_k_ff_2_qn));  // open: preset, en, reset
  Hex_Digit_Display hex_digit_display_1 (.value(j_k_ff_1_q));  // open: dp
  J_K_Flip_Flop j_k_ff_3 (
    .J(and_3_out), .clk(clock_1_out), .K(and_1_out), .Q(j_k_ff_1_q[2]), .Qn(j_k_ff_3_qn));  // open: preset, en, reset
  and and_3 (and_3_out, j_k_ff_1_q[3], j_k_ff_1_qn);
  and and_4 (and_4_out, j_k_ff_3_qn, and_1_out);
  J_K_Flip_Flop j_k_ff_4 (
    .J(and_4_out), .clk(clock_1_out), .K(j_k_ff_1_qn), .Q(j_k_ff_1_q[3]), .Qn(j_k_ff_4_qn));  // open: preset, en, reset
  or or_1 (or_1_out, j_k_ff_1_q[2], j_k_ff_1_q[3]);

  // Notes on the sheet:
  //   Q3Q2Q1Q0
  //   1010
  //   Q0
  //   q1
  //   q2
  //   q3
endmodule

module _99_00 (
);

  wire and_1_out, and_2_out, and_3_out, clock_1_out, d_ff_1_qn, d_ff_2_qn, d_ff_3_qn, d_ff_4_qn, d_ff_5_qn,
       d_ff_6_qn, d_ff_7_qn, d_ff_8_qn;
  wire [3:0] d_ff_1_q, d_ff_5_q;

  Clock clock_1 (.out(clock_1_out));
  D_Flip_Flop d_ff_1 (
    .clk(and_2_out), .D(d_ff_1_qn), .Q(d_ff_1_q[0]), .Qn(d_ff_1_qn), .reset(and_1_out));  // open: preset, en
  D_Flip_Flop d_ff_2 (
    .clk(d_ff_1_qn), .D(d_ff_2_qn), .Q(d_ff_1_q[1]), .Qn(d_ff_2_qn), .reset(and_1_out));  // open: preset, en
  Hex_Digit_Display hex_digit_display_1 (.value(d_ff_1_q));  // open: dp
  and and_1 (and_1_out, d_ff_1_q[1], d_ff_1_q[3]);
  D_Flip_Flop d_ff_3 (
    .clk(d_ff_2_qn), .D(d_ff_3_qn), .Q(d_ff_1_q[2]), .Qn(d_ff_3_qn), .reset(and_1_out));  // open: preset, en
  D_Flip_Flop d_ff_4 (
    .clk(d_ff_3_qn), .D(d_ff_4_qn), .Q(d_ff_1_q[3]), .Qn(d_ff_4_qn), .reset(and_1_out));  // open: preset, en
  and and_2 (and_2_out, clock_1_out, d_ff_5_q[1], d_ff_5_q[3]);
  D_Flip_Flop d_ff_5 (
    .clk(clock_1_out), .D(d_ff_5_qn), .Q(d_ff_5_q[0]), .Qn(d_ff_5_qn), .reset(and_3_out));  // open: preset, en
  Hex_Digit_Display hex_digit_display_2 (.value(d_ff_5_q));  // open: dp
  D_Flip_Flop d_ff_6 (
    .clk(d_ff_5_qn), .D(d_ff_6_qn), .Q(d_ff_5_q[1]), .Qn(d_ff_6_qn), .reset(and_3_out));  // open: preset, en
  and and_3 (and_3_out, d_ff_5_q[1], d_ff_5_q[3]);
  D_Flip_Flop d_ff_7 (
    .clk(d_ff_6_qn), .D(d_ff_7_qn), .Q(d_ff_5_q[2]), .Qn(d_ff_7_qn), .reset(and_3_out));  // open: preset, en
  D_Flip_Flop d_ff_8 (
    .clk(d_ff_7_qn), .D(d_ff_8_qn), .Q(d_ff_5_q[3]), .Qn(d_ff_8_qn), .reset(and_3_out));  // open: preset, en
endmodule

module _59_00 (
);

  wire and_1_out, and_2_out, and_3_out, clock_1_out, d_ff_1_qn, d_ff_2_qn, d_ff_3_qn, d_ff_5_qn, d_ff_6_qn,
       d_ff_7_qn, d_ff_8_qn;
  wire [3:0] d_ff_1_q, d_ff_5_q;

  Clock clock_1 (.out(clock_1_out));
  D_Flip_Flop d_ff_1 (
    .clk(and_2_out), .D(d_ff_1_qn), .Q(d_ff_1_q[0]), .Qn(d_ff_1_qn), .reset(and_1_out));  // open: preset, en
  D_Flip_Flop d_ff_2 (
    .clk(d_ff_1_qn), .D(d_ff_2_qn), .Q(d_ff_1_q[1]), .Qn(d_ff_2_qn), .reset(and_1_out));  // open: preset, en
  Hex_Digit_Display hex_digit_display_1 (.value(d_ff_1_q));  // open: dp
  and and_1 (and_1_out, d_ff_1_q[1], d_ff_1_q[1], d_ff_1_q[2]);
  D_Flip_Flop d_ff_3 (
    .clk(d_ff_2_qn), .D(d_ff_3_qn), .Q(d_ff_1_q[2]), .Qn(d_ff_3_qn), .reset(and_1_out));  // open: preset, en
  D_Flip_Flop d_ff_4 (.clk(d_ff_3_qn), .Q(d_ff_1_q[3]), .en(and_1_out));  // open: D, Qn, preset, reset
  and and_2 (and_2_out, clock_1_out, d_ff_5_q[1], d_ff_5_q[3]);
  D_Flip_Flop d_ff_5 (
    .clk(clock_1_out), .D(d_ff_5_qn), .Q(d_ff_5_q[0]), .Qn(d_ff_5_qn), .reset(and_3_out));  // open: preset, en
  Hex_Digit_Display hex_digit_display_2 (.value(d_ff_5_q));  // open: dp
  D_Flip_Flop d_ff_6 (
    .clk(d_ff_5_qn), .D(d_ff_6_qn), .Q(d_ff_5_q[1]), .Qn(d_ff_6_qn), .reset(and_3_out));  // open: preset, en
  and and_3 (and_3_out, d_ff_5_q[1], d_ff_5_q[3]);
  D_Flip_Flop d_ff_7 (
    .clk(d_ff_6_qn), .D(d_ff_7_qn), .Q(d_ff_5_q[2]), .Qn(d_ff_7_qn), .reset(and_3_out));  // open: preset, en
  D_Flip_Flop d_ff_8 (
    .clk(d_ff_7_qn), .D(d_ff_8_qn), .Q(d_ff_5_q[3]), .Qn(d_ff_8_qn), .reset(and_3_out));  // open: preset, en
endmodule

module _99_0_JK (
);

  wire and_1_out, and_2_out, and_3_out, and_4_out, and_5_out, and_6_out, and_7_out, and_8_out, clock_1_out,
       j_k_ff_1_qn, j_k_ff_2_qn, j_k_ff_3_qn, j_k_ff_5_qn, j_k_ff_6_qn, j_k_ff_7_qn, or_1_out, or_2_out;
  wire [3:0] j_k_ff_1_q, j_k_ff_5_q;

  J_K_Flip_Flop j_k_ff_1 (
    .J(1'b1), .clk(j_k_ff_5_q[3]), .K(1'b1), .Q(j_k_ff_1_q[0]), .Qn(j_k_ff_1_qn));  // open: preset, en, reset
  and and_1 (and_1_out, j_k_ff_1_qn, j_k_ff_2_qn);
  and and_2 (and_2_out, and_1_out, or_1_out);
  J_K_Flip_Flop j_k_ff_2 (
    .J(and_2_out), .clk(j_k_ff_5_q[3]), .K(j_k_ff_1_qn), .Q(j_k_ff_1_q[1]), .Qn(j_k_ff_2_qn));  // open: preset, en, reset
  J_K_Flip_Flop j_k_ff_3 (
    .J(and_3_out), .clk(j_k_ff_5_q[3]), .K(and_1_out), .Q(j_k_ff_1_q[2]), .Qn(j_k_ff_3_qn));  // open: preset, en, reset
  and and_3 (and_3_out, j_k_ff_1_q[3], j_k_ff_1_qn);
  and and_4 (and_4_out, j_k_ff_3_qn, and_1_out);
  J_K_Flip_Flop j_k_ff_4 (
    .J(and_4_out), .clk(j_k_ff_5_q[3]), .K(j_k_ff_1_qn), .Q(j_k_ff_1_q[3]));  // open: Qn, preset, en, reset
  or or_1 (or_1_out, j_k_ff_1_q[2], j_k_ff_1_q[3]);
  Hex_Digit_Display hex_digit_display_1 (.value(j_k_ff_1_q));  // open: dp
  Clock clock_1 (.out(clock_1_out));
  Hex_Digit_Display hex_digit_display_2 (.value(j_k_ff_5_q));  // open: dp
  J_K_Flip_Flop j_k_ff_5 (
    .J(1'b1), .clk(clock_1_out), .K(1'b1), .Q(j_k_ff_5_q[0]), .Qn(j_k_ff_5_qn));  // open: preset, en, reset
  and and_5 (and_5_out, j_k_ff_5_qn, j_k_ff_6_qn);
  and and_6 (and_6_out, and_5_out, or_2_out);
  J_K_Flip_Flop j_k_ff_6 (
    .J(and_6_out), .clk(clock_1_out), .K(j_k_ff_5_qn), .Q(j_k_ff_5_q[1]), .Qn(j_k_ff_6_qn));  // open: preset, en, reset
  J_K_Flip_Flop j_k_ff_7 (
    .J(and_7_out), .clk(clock_1_out), .K(and_5_out), .Q(j_k_ff_5_q[2]), .Qn(j_k_ff_7_qn));  // open: preset, en, reset
  and and_7 (and_7_out, j_k_ff_5_q[3], j_k_ff_5_qn);
  and and_8 (and_8_out, j_k_ff_7_qn, and_5_out);
  J_K_Flip_Flop j_k_ff_8 (
    .J(and_8_out), .clk(clock_1_out), .K(j_k_ff_5_qn), .Q(j_k_ff_5_q[3]));  // open: Qn, preset, en, reset
  or or_2 (or_2_out, j_k_ff_5_q[2], j_k_ff_5_q[3]);

  // Notes on the sheet:
  //   Q3Q2Q1Q0
  //   1010
  //   Q0
  //   q1
  //   q2
  //   q3
  //   Q0
  //   q1
  //   q2
  //   q3
endmodule

module _59_0_JK (
);

  wire and_1_out, and_2_out, and_3_out, and_4_out, and_5_out, and_6_out, and_7_out, and_8_out, clock_1_out,
       j_k_ff_1_qn, j_k_ff_2_qn, j_k_ff_3_qn, j_k_ff_5_qn, j_k_ff_6_qn, j_k_ff_7_qn, or_1_out, or_2_out;
  wire [3:0] j_k_ff_1_q, j_k_ff_5_q;

  J_K_Flip_Flop j_k_ff_1 (
    .J(1'b1), .clk(j_k_ff_5_q[3]), .K(1'b1), .Q(j_k_ff_1_q[0]), .Qn(j_k_ff_1_qn));  // open: preset, en, reset
  and and_1 (and_1_out, j_k_ff_1_qn, j_k_ff_2_qn);
  and and_2 (and_2_out, and_1_out, or_1_out);
  J_K_Flip_Flop j_k_ff_2 (
    .J(and_2_out), .clk(j_k_ff_5_q[3]), .K(j_k_ff_1_qn), .Q(j_k_ff_1_q[1]), .Qn(j_k_ff_2_qn));  // open: preset, en, reset
  J_K_Flip_Flop j_k_ff_3 (
    .J(and_3_out), .clk(j_k_ff_5_q[3]), .K(and_1_out), .Q(j_k_ff_1_q[2]), .Qn(j_k_ff_3_qn));  // open: preset, en, reset
  and and_3 (and_3_out, j_k_ff_1_q[3], j_k_ff_1_qn);
  and and_4 (and_4_out, j_k_ff_3_qn, and_1_out);
  J_K_Flip_Flop j_k_ff_4 (
    .J(and_4_out), .clk(j_k_ff_5_q[3]), .K(j_k_ff_1_qn), .Q(j_k_ff_1_q[3]));  // open: Qn, preset, en, reset
  or or_1 (or_1_out, j_k_ff_1_q[2], j_k_ff_1_q[3]);
  Hex_Digit_Display hex_digit_display_1 (.value(j_k_ff_1_q));  // open: dp
  Clock clock_1 (.out(clock_1_out));
  Hex_Digit_Display hex_digit_display_2 (.value(j_k_ff_5_q));  // open: dp
  J_K_Flip_Flop j_k_ff_5 (
    .J(1'b1), .clk(clock_1_out), .K(1'b1), .Q(j_k_ff_5_q[0]), .Qn(j_k_ff_5_qn));  // open: preset, en, reset
  and and_5 (and_5_out, j_k_ff_5_qn, j_k_ff_6_qn);
  and and_6 (and_6_out, and_5_out, or_2_out);
  J_K_Flip_Flop j_k_ff_6 (
    .J(and_6_out), .clk(clock_1_out), .K(j_k_ff_5_qn), .Q(j_k_ff_5_q[1]), .Qn(j_k_ff_6_qn));  // open: preset, en, reset
  J_K_Flip_Flop j_k_ff_7 (
    .J(and_7_out), .clk(clock_1_out), .K(and_5_out), .Q(j_k_ff_5_q[2]), .Qn(j_k_ff_7_qn));  // open: preset, en, reset
  and and_7 (and_7_out, j_k_ff_5_q[3], j_k_ff_5_qn);
  and and_8 (and_8_out, j_k_ff_7_qn, and_5_out);
  J_K_Flip_Flop j_k_ff_8 (
    .J(and_8_out), .clk(clock_1_out), .K(j_k_ff_5_qn), .Q(j_k_ff_5_q[3]));  // open: Qn, preset, en, reset
  or or_2 (or_2_out, j_k_ff_5_q[2], j_k_ff_5_q[3]);

  // Notes on the sheet:
  //   Q3Q2Q1Q0
  //   1010
  //   Q0
  //   q1
  //   q2
  //   q3
  //   Q0
  //   q1
  //   q2
  //   q3
endmodule
