// Logisim project 523H0102_NgoChiThuan_Countdown.circ as structural Verilog: 2 circuits, main circuit 9-0
module _9_0 (
  input  in_1
);

  wire and_1_out, and_2_out, and_3_out, and_4_out, clock_1_out, j_k_ff_1_qn, j_k_ff_2_qn, j_k_ff_3_qn,
       or_1_out;
  wire [3:0] j_k_ff_1_q;

  Clock clock_1 (.out(clock_1_out));
  and and_1 (and_1_out, j_k_ff_1_qn, j_k_ff_2_qn);
  J_K_Flip_Flop j_k_ff_1 (
    .J(in_1), .clk(clock_1_out), .K(in_1), .Q(j_k_ff_1_q[0]), .Qn(j_k_ff_1_qn));  // open: preset, en, reset
  and and_2 (and_2_out, and_1_out, or_1_out);
  J_K_Flip_Flop j_k_ff_2 (
    .J(and_2_out), .clk(clock_1_out), .K(j_k_ff_1_qn), .Q(j_k_ff_1_q[1]), .Qn(j_k_ff_2_qn));  // open: preset, en, reset
  J_K_Flip_Flop j_k_ff_3 (
    .J(and_3_out), .clk(clock_1_out), .K(and_1_out), .Q(j_k_ff_1_q[2]), .Qn(j_k_ff_3_qn));  // open: preset, en, reset
  and and_3 (and_3_out, j_k_ff_1_q[3], j_k_ff_1_qn);
  and and_4 (and_4_out, j_k_ff_3_qn, and_1_out);
  J_K_Flip_Flop j_k_ff_4 (
    .J(and_4_out), .clk(clock_1_out), .K(j_k_ff_1_qn), .Q(j_k_ff_1_q[3]));  // open: Qn, preset, en, reset
  or or_1 (or_1_out, j_k_ff_1_q[2], j_k_ff_1_q[3]);
  Hex_Digit_Display hex_digit_display_1 (.value(j_k_ff_1_q));  // open: dp
endmodule

module _99_0 (
  input  in_1,
  input  in_2
);

  wire and_1_out, and_2_out, and_3_out, and_4_out, and_5_out, and_6_out, and_7_out, and_8_out, clock_1_out,
       j_k_ff_1_qn, j_k_ff_2_qn, j_k_ff_3_qn, j_k_ff_4_qn, j_k_ff_5_qn, j_k_ff_6_qn, or_1_out, or_2_out;
  wire [3:0] j_k_ff_1_q, j_k_ff_2_q;

  Clock clock_1 (.out(clock_1_out));
  and and_1 (and_1_out, j_k_ff_1_qn, j_k_ff_3_qn);
  and and_2 (and_2_out, j_k_ff_2_qn, j_k_ff_4_qn);
  J_K_Flip_Flop j_k_ff_1 (
    .J(in_1), .clk(clock_1_out), .K(in_1), .Q(j_k_ff_1_q[0]), .Qn(j_k_ff_1_qn));  // open: preset, en, reset
  J_K_Flip_Flop j_k_ff_2 (
    .J(in_2), .clk(j_k_ff_1_q[3]), .K(in_2), .Q(j_k_ff_2_q[0]), .Qn(j_k_ff_2_qn));  // open: preset, en, reset
  and and_3 (and_3_out, and_1_out, or_1_out);
  and and_4 (and_4_out, and_2_out, or_2_out);
  J_K_Flip_Flop j_k_ff_3 (
    .J(and_3_out), .clk(clock_1_out), .K(j_k_ff_1_qn), .Q(j_k_ff_1_q[1]), .Qn(j_k_ff_3_qn));  // open: preset, en, reset
  J_K_Flip_Flop j_k_ff_4 (
    .J(and_4_out), .clk(j_k_ff_1_q[3]), .K(j_k_ff_2_qn), .Q(j_k_ff_2_q[1]), .Qn(j_k_ff_4_qn));  // open: preset, en, reset
  J_K_Flip_Flop j_k_ff_5 (
    .J(and_5_out), .clk(clock_1_out), .K(and_1_out), .Q(j_k_ff_1_q[2]), .Qn(j_k_ff_5_qn));  // open: preset, en, reset
  J_K_Flip_Flop j_k_ff_6 (
    .J(and_7_out), .clk(j_k_ff_1_q[3]), .K(and_2_out), .Q(j_k_ff_2_q[2]), .Qn(j_k_ff_6_qn));  // open: preset, en, reset
  and and_5 (and_5_out, j_k_ff_1_q[3], j_k_ff_1_qn);
  and and_6 (and_6_out, j_k_ff_5_qn, and_1_out);
  and and_7 (and_7_out, j_k_ff_2_q[3], j_k_ff_2_qn);
  and and_8 (and_8_out, j_k_ff_6_qn, and_2_out);
  J_K_Flip_Flop j_k_ff_7 (
    .J(and_6_out), .clk(clock_1_out), .K(j_k_ff_1_qn), .Q(j_k_ff_1_q[3]));  // open: Qn, preset, en, reset
  or or_1 (or_1_out, j_k_ff_1_q[2], j_k_ff_1_q[3]);
  J_K_Flip_Flop j_k_ff_8 (
    .J(and_8_out), .clk(j_k_ff_1_q[3]), .K(j_k_ff_2_qn), .Q(j_k_ff_2_q[3]));  // open: Qn, preset, en, reset
  or or_2 (or_2_out, j_k_ff_2_q[2], j_k_ff_2_q[3]);
  Hex_Digit_Display hex_digit_display_1 (.value(j_k_ff_1_q));  // open: dp
  Hex_Digit_Display hex_digit_display_2 (.value(j_k_ff_2_q));  // open: dp
endmodule
